# Fritzing sketch rocker (saved by Fritzing 0.9.3b)
circuit board: 3.89088cm x 6.09723cm
circuit board: 2.1894cm x 1.70579cm
circuit board: 3.32122cm x 3.23337cm
circuit board: 1.89919cm x 6.81071cm
circuit board: 7.21078cm x 9.25619cm

parts:
  S1 = SWITCH-MOMENTARY-2 [part_number="Fob A" package=tactile-switch-1101ne]
  BAT1 = Battery Holders [part_number=keyfob-holder package=battcom_20mm_pth]
  S3 = SPST Switch [part_number=Microswitch package=switch-spst-smd-a]
  ItsyBitsy = Itsy Bitsy 32u4 5V @ 16MHz [part_number="Adafruit #3677"]
  BAT2 = Battery Holders [part_number=18650 package=battery-aa]
  R1 = Resistor [tolerance=±5% resistance=1k package=THT]
  Q1 = TRANSISTOR_NPN [part_number=pn2222a package=to-92]
  flipped_tps61203 = Micro Lipo Charger

nets:
  N1: S1.1, BAT1.+
  N2: S1.2, Q1.E
  GND: BAT1.-, S3.S, ItsyBitsy.GND, BAT2.-, flipped_tps61203.GND
  N3: S3.P, ItsyBitsy.D7
  Vcc: ItsyBitsy.VBUS, Q1.C, flipped_tps61203.5V
  N4: ItsyBitsy.D5, R1.Pin_0
  N5: BAT2.+, flipped_tps61203.VBAT
  N6: R1.Pin_1, Q1.B

notes:
  https://cdn-shop.adafruit.com/datasheets/PT2272.pdf
  https://www.renesas.com/us/en/document/dst/icm7555-icm7556-datasheet
  keyfob

custom parts:
  Itsy Bitsy 32u4 5V @ 16MHz: What's smaller than a Feather but larger than a Trinket? It's an Itsy Bitsy! Small, powerful, Arduino-compatible - this microcontroller board is perfect when you want something very compact, but still with a bunch of pins. Itsy Bitsy is only 1.4" long by 0.7" wide, but has 6 power pins, 6 analog & digital pins and 17 digital pins. It packs much of the same capability as an Arduino UNO. So it's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
  Micro Lipo Charger: Oh so handy, this little lipo charger is so small and easy to use you can keep it on your desk or mount it easily into any project! Simply plug it via any MicroUSB cable into a USB port and a 3.7V/4.2V lithium polymer or lithium ion rechargeable battery into the JST plug on the other end. There are two LEDs - one red and one green. While charging, the red LED is lit. When the battery is fully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
